// Digital circuit BaseCircuits.dig as structural Verilog
module BaseCircuits (
);

  wire A_2_p3, A_3_p3, A_b, B_2_p3, B_3_p3, B_b, Buffer_C_In_p3, C_In_2_b, C_In_3_b, C_In_p3, Clk_2_b,
       Clk_3_b, Clk_b, I_b, R_b, relaydt_1_p1, relaydt_1_p4, relaydt_2_p3, relaydt_3_p3, relaydt_3_p4,
       relaydt_3_p5, relaydt_3_p7, relaydt_4_p4, relaydt_4_p5, relaydt_6_p5, relaydt_7_p4, relaydt_8_p2,
       relaydt_10_p1, relaydt_12_p1, relaydt_12_p4, relaydt_14_p4, relaydt_14_p5, relaydt_14_p7,
       relaydt_15_p4, relaydt_15_p7, relaydt_16_p5, relaydt_16_p6, relaydt_17_p4, relaydt_17_p5,
       relaydt_17_p7, relaydt_18_p4, relaydt_19_p5, relaydt_19_p6, relaydt_20_p3, relaydt_20_p6,
       relaydt_20_p7, S_b;

  Switch S (.A(1'b1), .B(S_b));
  Switch R (.A(1'b1), .B(R_b));
  Switch Clk (.A(1'b1), .B(Clk_b));
  Switch Clk_2 (.A(1'b1), .B(Clk_2_b));
  // RelayDT relaydt_1: pin names not known; wires that end beside it: relaydt_1_p1, 1'b0, 1'b1, relaydt_1_p4
  // RelayDT relaydt_2: pin names not known; wires that end beside it: Clk_b, 1'b0, relaydt_2_p3, relaydt_1_p1, relaydt_1_p4
  // RelayDT #(.poles(2)) relaydt_3: pin names not known; wires that end beside it: Clk_2_b, 1'b0, relaydt_3_p3, relaydt_3_p4, relaydt_3_p5, relaydt_3_p3, relaydt_3_p7
  // RelayDT relaydt_4: pin names not known; wires that end beside it: S_b, 1'b0, S_b, relaydt_4_p4, relaydt_4_p5
  // RelayDT relaydt_5: pin names not known; wires that end beside it: R_b, 1'b0, relaydt_4_p5, 1'b1, relaydt_4_p4
  LightBulb Q_plus (.A(relaydt_1_p4), .B(1'b0));
  // RelayDT #(.poles(2)) relaydt_6: pin names not known; wires that end beside it: relaydt_3_p4, 1'b0, 1'b1, relaydt_3_p5, relaydt_6_p5, 1'b1
  LightBulb Q (.A(S_b), .B(1'b0));
  LightBulb nQ (.A(relaydt_4_p5), .B(1'b0));
  // RelayDT relaydt_7: pin names not known; wires that end beside it: relaydt_1_p4, 1'b0, Clk_b, relaydt_7_p4, 1'b1, 1'b1
  // RelayDT relaydt_8: pin names not known; wires that end beside it: 1'b0, relaydt_8_p2
  // RelayDT relaydt_9: pin names not known; wires that end beside it: relaydt_6_p5, relaydt_3_p3, relaydt_3_p7, 1'b1, 1'b0
  LightBulb nQ_plus (.A(relaydt_7_p4), .B(1'b0));
  LightBulb Q_plus_2 (.A(relaydt_3_p5), .B(1'b0));
  LightBulb nQ_plus_2 (.A(relaydt_6_p5), .B(1'b0));
  LightBulb Q_2 (.A(relaydt_3_p3), .B(1'b0));
  Switch I (.A(1'b1), .B(I_b));
  Switch Clk_3 (.A(1'b1), .B(Clk_3_b));
  // RelayDT relaydt_10: pin names not known; wires that end beside it: relaydt_10_p1, 1'b0, 1'b1, relaydt_2_p3
  // RelayDT relaydt_11: pin names not known; wires that end beside it: relaydt_8_p2, 1'b0, relaydt_7_p4, relaydt_10_p1, relaydt_2_p3
  LightBulb Q_3 (.A(relaydt_2_p3), .B(1'b0));
  // RelayDT relaydt_12: pin names not known; wires that end beside it: relaydt_12_p1, 1'b0, 1'b1, relaydt_12_p4
  // RelayDT relaydt_13: pin names not known; wires that end beside it: Clk_3_b, 1'b0, I_b, relaydt_12_p1, relaydt_12_p4
  LightBulb Q_4 (.A(relaydt_12_p4), .B(1'b0));
  Switch A (.A(1'b1), .B(A_b));
  Switch B (.A(1'b1), .B(B_b));
  // SwitchDT C_In: pin names not known; wires that end beside it: 1'b1, 1'b0, C_In_p3, C_In_p3
  // SwitchDT A_2: pin names not known; wires that end beside it: 1'b1, 1'b0, A_2_p3
  // SwitchDT B_2: pin names not known; wires that end beside it: 1'b1, 1'b0, B_2_p3
  // RelayDT #(.poles(2)) relaydt_14: pin names not known; wires that end beside it: A_b, 1'b0, 1'b1, relaydt_14_p4, relaydt_14_p5, 1'b1, relaydt_14_p7
  // RelayDT #(.poles(2)) relaydt_15: pin names not known; wires that end beside it: B_b, 1'b0, relaydt_14_p5, relaydt_15_p4, relaydt_14_p4, relaydt_14_p7, relaydt_15_p7
  // RelayDT #(.poles(2)) relaydt_16: pin names not known; wires that end beside it: 1'b1, 1'b0, 1'b0, 1'b1, relaydt_16_p5, relaydt_16_p6, 1'b0
  Switch C_In_2 (.A(1'b1), .B(C_In_2_b));
  // SwitchDT Buffer_C_In: pin names not known; wires that end beside it: relaydt_16_p6, C_In_p3, Buffer_C_In_p3, Buffer_C_In_p3
  // RelayDT #(.poles(2)) relaydt_17: pin names not known; wires that end beside it: relaydt_15_p4, 1'b0, 1'b1, relaydt_17_p4, relaydt_17_p5, 1'b1, relaydt_17_p7
  // RelayDT #(.poles(2)) relaydt_18: pin names not known; wires that end beside it: C_In_2_b, 1'b0, relaydt_17_p5, relaydt_18_p4, relaydt_17_p4, relaydt_17_p7, relaydt_15_p7
  // RelayDT #(.poles(2)) relaydt_19: pin names not known; wires that end beside it: relaydt_16_p5, A_2_p3, Buffer_C_In_p3, A_2_p3, relaydt_19_p5, relaydt_19_p6, B_2_p3
  LightBulb Sum (.A(relaydt_19_p5), .B(1'b0));
  LightBulb C_Out (.A(relaydt_19_p6), .B(1'b0));
  LightBulb C_Out_2 (.A(relaydt_15_p7), .B(1'b0));
  LightBulb Sum_2 (.A(relaydt_18_p4), .B(1'b0));
  // SwitchDT A_3: pin names not known; wires that end beside it: 1'b1, 1'b0, A_3_p3
  // SwitchDT B_3: pin names not known; wires that end beside it: 1'b1, 1'b0, B_3_p3
  Switch C_In_3 (.A(1'b1), .B(C_In_3_b));
  // RelayDT #(.poles(2)) relaydt_20: pin names not known; wires that end beside it: A_3_p3, B_3_p3, relaydt_20_p3, C_In_3_b, B_3_p3, relaydt_20_p6, relaydt_20_p7, C_In_3_b
  // RelayDT relaydt_21: pin names not known; wires that end beside it: 1'b1, 1'b0, C_In_3_b, relaydt_20_p7, 1'b0
  LightBulb C_Out_3 (.A(relaydt_20_p3), .B(1'b0));
  LightBulb Sum_3 (.A(relaydt_20_p6), .B(1'b0));

  // Notes on the sheet:
  //   SR Latch
  //   Clocked Invert
  //   D Flip-Flop
  //   On +Clk Q+ inverts
  //   On -Clk Q- inverts
  //   ~Q+ is always inverse of Q+
  //   Works by latching the value of Q- into
  //   the first D F-F on +Clk and latching the
  //   value of Q+ into the second D FF on
  //   -Clk. The two relays in the middle
  //   invert Clk and Q from the first D F-F.
  //   Full Adder
  //   cube#8694's Full Adder
  //   cube#8694's Full Adder (Modified)
  //   Timings:
  //   A/B to Sum: 2
  //   C_In to Sum: 1
  //   A/B to C_Out if C_In == 0: 1
  //   A/B to C_Out if C_In == 1: 2
  //   C_In to C_Out: 1
  //   (assuming A/B and C_In change separately)
  //   Timings:
  //   A/B to Sum: 1
  //   C_In to Sum if A XOR B: 1
  //   C_In to Sum if A XNOR B: 0
  //   A/B to C_Out: 1
  //   C_In to C_Out: 0
  //   (assuming A/B and C_In change separately)
endmodule
