// Digital circuit ClockedInvert.dig as structural Verilog
// On +Clk Q+ inverts
// On -Clk Q- inverts
// When Clk is 0, Q+ and Q- are inverse
// Outputs are Vdd/Z
module ClockedInvert (
  input  Clk,
  output Q_plus,
  output nQ_plus,
  output Q,
  output nQ
);

  wire relaydt_1_p1, relaydt_2_p7;

  // RelayDT #(.poles(2)) relaydt_1: pin names not known; wires that end beside it: relaydt_1_p1, 1'b0, 1'b1, Q_plus, nQ_plus, 1'b1
  // RelayDT #(.poles(2)) relaydt_2: pin names not known; wires that end beside it: Clk, 1'b0, Q, relaydt_1_p1, Q_plus, Q, relaydt_2_p7, nQ_plus
  // RelayDT relaydt_3: pin names not known; wires that end beside it: nQ, Q, relaydt_2_p7, 1'b1, 1'b0

  // Notes on the sheet:
  //   On +Clk Q+ inverts
  //   On -Clk Q- inverts
  //   When Clk is 0, Q+ and Q- are inverse
  //   Outputs are Vdd/Z
  //   Works by latching the value of Q- into
  //   the first D F-F on +Clk and latching the
  //   value of Q+ into the second D FF on
  //   -Clk. The two relays in the middle
  //   invert Clk and Q from the first D F-F.
endmodule
