// Digital circuit Counter4.dig as structural Verilog
module Counter4 (
  input  Clk,
  output Out_0,
  output Out_1,
  output Out_2,
  output Out_3,
  output Clk_Carry
);

  wire relaydt_1_p1, relaydt_2_p3, relaydt_3_p1, relaydt_4_p1, relaydt_4_p3, relaydt_5_p1, relaydt_6_p1,
       relaydt_6_p3, relaydt_7_p1, relaydt_8_p1, relaydt_8_p3, relaydt_10_p3, relaydt_14_p1, relaydt_16_p1,
       relaydt_18_p1, relaydt_20_p1;

  // RelayDT relaydt_1: pin names not known; wires that end beside it: relaydt_1_p1, 1'b0, 1'b1, Out_0
  // RelayDT relaydt_2: pin names not known; wires that end beside it: Clk, 1'b0, relaydt_2_p3, relaydt_1_p1
  // RelayDT relaydt_3: pin names not known; wires that end beside it: relaydt_3_p1, 1'b0, 1'b1, Out_1
  // RelayDT relaydt_4: pin names not known; wires that end beside it: relaydt_4_p1, 1'b0, relaydt_4_p3, relaydt_3_p1
  // RelayDT relaydt_5: pin names not known; wires that end beside it: relaydt_5_p1, 1'b0, 1'b1, Out_2
  // RelayDT relaydt_6: pin names not known; wires that end beside it: relaydt_6_p1, 1'b0, relaydt_6_p3, relaydt_5_p1
  // RelayDT relaydt_7: pin names not known; wires that end beside it: relaydt_7_p1, 1'b0, 1'b1, Out_3
  // RelayDT relaydt_8: pin names not known; wires that end beside it: relaydt_8_p1, 1'b0, relaydt_8_p3, relaydt_7_p1
  // RelayDT relaydt_9: pin names not known; wires that end beside it: relaydt_1_p1, 1'b0, relaydt_4_p1, 1'b1
  // RelayDT relaydt_10: pin names not known; wires that end beside it: Clk, 1'b0, relaydt_10_p3, 1'b1
  // RelayDT relaydt_11: pin names not known; wires that end beside it: relaydt_3_p1, 1'b0, relaydt_6_p1, 1'b1
  // RelayDT relaydt_12: pin names not known; wires that end beside it: relaydt_5_p1, 1'b0, relaydt_8_p1, 1'b1
  // RelayDT relaydt_13: pin names not known; wires that end beside it: relaydt_7_p1, 1'b0, Clk_Carry, 1'b1
  // RelayDT relaydt_14: pin names not known; wires that end beside it: relaydt_14_p1, 1'b0, 1'b1, relaydt_2_p3
  // RelayDT relaydt_15: pin names not known; wires that end beside it: relaydt_10_p3, 1'b0, relaydt_4_p1, relaydt_14_p1, relaydt_2_p3
  // RelayDT relaydt_16: pin names not known; wires that end beside it: relaydt_16_p1, 1'b0, 1'b1, relaydt_4_p3
  // RelayDT relaydt_17: pin names not known; wires that end beside it: Out_0, 1'b0, relaydt_6_p1, relaydt_16_p1, relaydt_4_p3
  // RelayDT relaydt_18: pin names not known; wires that end beside it: relaydt_18_p1, 1'b0, 1'b1, relaydt_6_p3
  // RelayDT relaydt_19: pin names not known; wires that end beside it: Out_1, 1'b0, relaydt_8_p1, relaydt_18_p1, relaydt_6_p3
  // RelayDT relaydt_20: pin names not known; wires that end beside it: relaydt_20_p1, 1'b0, 1'b1, relaydt_8_p3
  // RelayDT relaydt_21: pin names not known; wires that end beside it: Out_2, 1'b0, Clk_Carry, relaydt_20_p1, relaydt_8_p3
endmodule
