// Digital circuit CounterPresettable4.dig as structural Verilog
module CounterPresettable4 (
  input  Clk,
  input  In0,
  input  Set,
  input  In1,
  input  In2,
  input  In3,
  output Out_0,
  output Out_1,
  output Out_2,
  output Out_3,
  output Clk_Carry
);

  wire relaydt_2_p1, relaydt_3_p3, relaydt_3_p4, relaydt_5_p1, relaydt_6_p1, relaydt_6_p3, relaydt_6_p4,
       relaydt_8_p1, relaydt_9_p1, relaydt_9_p3, relaydt_9_p4, relaydt_11_p1, relaydt_12_p1, relaydt_12_p3,
       relaydt_12_p4, relaydt_15_p3, relaydt_19_p1, relaydt_21_p1, relaydt_23_p1, relaydt_25_p1;

  // RelayDT relaydt_1: pin names not known; wires that end beside it: 1'b1, 1'b0
  // RelayDT relaydt_2: pin names not known; wires that end beside it: relaydt_2_p1, 1'b0, 1'b1, Out_0
  // RelayDT relaydt_3: pin names not known; wires that end beside it: Clk, 1'b0, relaydt_3_p3, relaydt_3_p4
  // RelayDT relaydt_4: pin names not known; wires that end beside it: Set, 1'b0, In0, relaydt_2_p1, relaydt_3_p4
  // RelayDT relaydt_5: pin names not known; wires that end beside it: relaydt_5_p1, 1'b0, 1'b1, Out_1
  // RelayDT relaydt_6: pin names not known; wires that end beside it: relaydt_6_p1, 1'b0, relaydt_6_p3, relaydt_6_p4
  // RelayDT relaydt_7: pin names not known; wires that end beside it: Set, 1'b0, In1, relaydt_5_p1, relaydt_6_p4
  // RelayDT relaydt_8: pin names not known; wires that end beside it: relaydt_8_p1, 1'b0, 1'b1, Out_2
  // RelayDT relaydt_9: pin names not known; wires that end beside it: relaydt_9_p1, 1'b0, relaydt_9_p3, relaydt_9_p4
  // RelayDT relaydt_10: pin names not known; wires that end beside it: Set, 1'b0, In2, relaydt_8_p1, relaydt_9_p4
  // RelayDT relaydt_11: pin names not known; wires that end beside it: relaydt_11_p1, 1'b0, 1'b1, Out_3
  // RelayDT relaydt_12: pin names not known; wires that end beside it: relaydt_12_p1, 1'b0, relaydt_12_p3, relaydt_12_p4
  // RelayDT relaydt_13: pin names not known; wires that end beside it: Set, 1'b0, In3, relaydt_11_p1, relaydt_12_p4
  // RelayDT relaydt_14: pin names not known; wires that end beside it: relaydt_2_p1, 1'b0, relaydt_6_p1, 1'b1
  // RelayDT relaydt_15: pin names not known; wires that end beside it: Clk, 1'b0, relaydt_15_p3, 1'b1
  // RelayDT relaydt_16: pin names not known; wires that end beside it: relaydt_5_p1, 1'b0, relaydt_9_p1, 1'b1
  // RelayDT relaydt_17: pin names not known; wires that end beside it: relaydt_8_p1, 1'b0, relaydt_12_p1, 1'b1
  // RelayDT relaydt_18: pin names not known; wires that end beside it: relaydt_11_p1, 1'b0, Clk_Carry, 1'b1
  // RelayDT relaydt_19: pin names not known; wires that end beside it: relaydt_19_p1, 1'b0, 1'b1, relaydt_3_p3
  // RelayDT relaydt_20: pin names not known; wires that end beside it: relaydt_15_p3, 1'b0, relaydt_6_p1, relaydt_19_p1, relaydt_3_p3
  // RelayDT relaydt_21: pin names not known; wires that end beside it: relaydt_21_p1, 1'b0, 1'b1, relaydt_6_p3
  // RelayDT relaydt_22: pin names not known; wires that end beside it: Out_0, 1'b0, relaydt_9_p1, relaydt_21_p1, relaydt_6_p3
  // RelayDT relaydt_23: pin names not known; wires that end beside it: relaydt_23_p1, 1'b0, 1'b1, relaydt_9_p3
  // RelayDT relaydt_24: pin names not known; wires that end beside it: Out_1, 1'b0, relaydt_12_p1, relaydt_23_p1, relaydt_9_p3
  // RelayDT relaydt_25: pin names not known; wires that end beside it: relaydt_25_p1, 1'b0, 1'b1, relaydt_12_p3
  // RelayDT relaydt_26: pin names not known; wires that end beside it: Out_2, 1'b0, Clk_Carry, relaydt_25_p1, relaydt_12_p3
endmodule
